// Logisim project ym2610.circ as structural Verilog: 17 circuits, main circuit ym2610
module ym2610 (
  input  in_1
);

  wire clk_gen_1_clk1, clk_gen_1_clk2, clock_1_out, controlled_buffer_1_out, controlled_buffer_9_out,
       not_1_out, not_2_out, undriven;
  wire [8:0] write_data_1_nvalout, write_data_1_valout;

  Clock clock_1 (.out(clock_1_out));
  clk_gen clk_gen_1 (.MCLK(clock_1_out), .clk1(clk_gen_1_clk1), .clk2(clk_gen_1_clk2));
  clk_div clk_div_1 (
    .clk1(clk_gen_1_clk1), .clk2(clk_gen_1_clk2), .IC(in_1));  // open: fm_clk1, fm_clk2, res_latch1, res_latch2, out_8, out_9, out_10, out_11, out_12, out_13, out_14
  // NOT_Gate not_1 has open pins: in=open, out=not_1_out
  not not_2 (not_2_out, not_1_out);
  write_data write_data_1 (
    .valout(write_data_1_valout), .nvalout(write_data_1_nvalout));  // open: data_in, bank, write, oe
  assign controlled_buffer_1_out = undriven ? write_data_1_valout[0] : 1'bz;  // Controlled_Buffer controlled_buffer_1
  assign controlled_buffer_1_out = undriven ? write_data_1_valout[1] : 1'bz;  // Controlled_Buffer controlled_buffer_2
  assign controlled_buffer_1_out = undriven ? write_data_1_valout[2] : 1'bz;  // Controlled_Buffer controlled_buffer_3
  assign controlled_buffer_1_out = undriven ? write_data_1_valout[3] : 1'bz;  // Controlled_Buffer controlled_buffer_4
  assign controlled_buffer_1_out = undriven ? write_data_1_valout[4] : 1'bz;  // Controlled_Buffer controlled_buffer_5
  assign controlled_buffer_1_out = undriven ? write_data_1_valout[5] : 1'bz;  // Controlled_Buffer controlled_buffer_6
  assign controlled_buffer_1_out = undriven ? write_data_1_valout[6] : 1'bz;  // Controlled_Buffer controlled_buffer_7
  assign controlled_buffer_1_out = undriven ? write_data_1_valout[7] : 1'bz;  // Controlled_Buffer controlled_buffer_8
  assign controlled_buffer_9_out = not_2_out ? write_data_1_nvalout[0] : 1'bz;  // Controlled_Buffer controlled_buffer_9
  assign controlled_buffer_9_out = not_2_out ? write_data_1_nvalout[1] : 1'bz;  // Controlled_Buffer controlled_buffer_10
  assign controlled_buffer_9_out = not_2_out ? write_data_1_nvalout[2] : 1'bz;  // Controlled_Buffer controlled_buffer_11
  assign controlled_buffer_9_out = not_2_out ? write_data_1_nvalout[3] : 1'bz;  // Controlled_Buffer controlled_buffer_12
  Controlled_Buffer controlled_buffer_13 (.out(controlled_buffer_9_out), .en(not_2_out));  // open: in
  assign controlled_buffer_9_out = not_2_out ? write_data_1_nvalout[5] : 1'bz;  // Controlled_Buffer controlled_buffer_14
  Controlled_Buffer controlled_buffer_15 (.out(controlled_buffer_9_out), .en(not_2_out));  // open: in
  Controlled_Buffer controlled_buffer_16 (.out(controlled_buffer_9_out), .en(not_2_out));  // open: in
  // also tied to GND on the sheet: {controlled_buffer_9_out, controlled_buffer_1_out}
endmodule

module sr_bit (
  input  val,
  input  clk1,
  input  clk2,
  output valout,
  output nvalout
);

  wire d_ff_1_q;

  D_Flip_Flop #(.trigger("high")) d_ff_1 (.D(val), .clk(clk1), .Q(d_ff_1_q));  // open: Qn, preset, reset
  D_Flip_Flop #(.trigger("high")) d_ff_2 (.D(d_ff_1_q), .clk(clk2), .Q(valout), .Qn(nvalout));  // open: preset, reset
endmodule

module reg_bit_1 (
  input  oe,
  input  val,
  input  write,
  output nvalout,
  output valout
);

  wire d_ff_1_q, nor_1_out, nor_2_out;

  D_Flip_Flop #(.trigger("high")) d_ff_1 (.D(val), .clk(write), .Q(d_ff_1_q));  // open: Qn, preset, reset
  nor nor_1 (nor_1_out, oe, d_ff_1_q);
  nor nor_2 (nor_2_out, oe, nor_1_out);
  assign nvalout = nor_1_out ? 1'b1 : 1'bz;  // Controlled_Buffer controlled_buffer_1
  assign nvalout = nor_2_out ? 1'b0 : 1'bz;  // Controlled_Buffer controlled_buffer_2
  assign valout = nor_2_out ? 1'b1 : 1'bz;  // Controlled_Buffer controlled_buffer_3
  assign valout = nor_1_out ? 1'b0 : 1'bz;  // Controlled_Buffer controlled_buffer_4

  // Notes on the sheet:
  //   dynamic latch!!!
endmodule

module read_bus_1 (
  input  val,
  input  enable,
  output valout
);

  wire nor_1_out, nor_2_out;

  nor nor_1 (nor_1_out, val, enable);
  nor nor_2 (nor_2_out, nor_1_out, enable);
  assign valout = nor_2_out ? 1'b1 : 1'bz;  // Controlled_Buffer controlled_buffer_1
  assign valout = nor_1_out ? 1'b0 : 1'bz;  // Controlled_Buffer controlled_buffer_2
endmodule

module write_data (
  input  [7:0] data_in,
  input  bank,
  input  write,
  input  oe,
  output [8:0] valout,
  output [8:0] nvalout
);

  reg_bit_1 reg_bit_1_1 (.oe(oe), .val(data_in[0]), .write(write), .nvalout(nvalout[0]), .valout(valout[0]));
  reg_bit_1 reg_bit_1_2 (.oe(oe), .val(data_in[1]), .write(write), .nvalout(nvalout[1]), .valout(valout[1]));
  reg_bit_1 reg_bit_1_3 (.oe(oe), .val(data_in[2]), .write(write), .nvalout(nvalout[2]), .valout(valout[2]));
  reg_bit_1 reg_bit_1_4 (.oe(oe), .val(data_in[3]), .write(write), .nvalout(nvalout[3]), .valout(valout[3]));
  reg_bit_1 reg_bit_1_5 (.oe(oe), .val(data_in[4]), .write(write), .nvalout(nvalout[4]), .valout(valout[4]));
  reg_bit_1 reg_bit_1_6 (.oe(oe), .val(data_in[5]), .write(write), .nvalout(nvalout[5]), .valout(valout[5]));
  reg_bit_1 reg_bit_1_7 (.oe(oe), .val(data_in[6]), .write(write), .nvalout(nvalout[6]), .valout(valout[6]));
  reg_bit_1 reg_bit_1_8 (.oe(oe), .val(data_in[7]), .write(write), .nvalout(nvalout[7]), .valout(valout[7]));
  reg_bit_1 reg_bit_1_9 (.oe(oe), .val(bank), .write(write), .nvalout(nvalout[8]), .valout(valout[8]));
endmodule

module clk_gen (
  input  MCLK,
  output clk1,
  output clk2
);

  wire not_1_out, not_2_out, not_3_out, not_4_out, not_5_out, not_6_out, not_7_out;

  not not_1 (not_1_out, MCLK);
  not not_2 (not_2_out, not_1_out);
  not not_3 (not_3_out, not_2_out);
  nor nor_1 (clk1, not_2_out, not_7_out);
  nor nor_2 (clk2, not_3_out, not_6_out);
  not not_4 (not_4_out, clk1);
  not not_5 (not_5_out, clk2);
  not not_6 (not_6_out, not_4_out);
  not not_7 (not_7_out, not_5_out);
endmodule

module clk_div (
  input  clk1,
  input  clk2,
  input  IC,
  output fm_clk1,
  output fm_clk2,
  output res_latch1,
  output res_latch2,
  output out_8,
  output out_9,
  output out_10,
  output out_11,
  output out_12,
  output out_13,
  output out_14
);

  wire nor_1_out, nor_2_out, nor_3_out, nor_4_out, nor_5_out, nor_6_out, nor_7_out, nor_8_out, nor_9_out,
       nor_10_out, nor_11_out, not_1_out, not_2_out, not_3_out, not_6_out, not_9_out, not_12_out, not_13_out,
       not_14_out, not_15_out, not_16_out, not_17_out, not_18_out, not_19_out, not_20_out, sr_bit_1_valout,
       sr_bit_2_valout, sr_bit_3_valout, sr_bit_4_valout, sr_bit_5_valout, sr_bit_6_valout, sr_bit_7_valout,
       sr_bit_8_valout, sr_bit_9_valout, sr_bit_10_valout, sr_bit_11_valout, sr_bit_12_valout,
       sr_bit_13_valout, sr_bit_14_valout, sr_bit_15_valout, sr_bit_16_valout, sr_bit_17_valout,
       sr_bit_18_valout, sr_bit_19_valout, sr_bit_20_valout, sr_bit_21_valout, sr_bit_22_valout,
       sr_bit_23_valout, sr_bit_24_valout, sr_bit_25_valout, sr_bit_26_valout, sr_bit_27_valout,
       sr_bit_28_valout, sr_bit_29_valout, sr_bit_30_valout, sr_bit_31_valout, sr_bit_32_valout,
       sr_bit_33_valout, sr_bit_34_valout, sr_bit_35_valout, sr_bit_36_valout, sr_bit_37_valout,
       sr_bit_38_valout, sr_bit_39_valout, sr_bit_40_valout, sr_bit_41_valout, sr_bit_42_valout;

  sr_bit sr_bit_1 (.clk1(clk1), .clk2(clk2), .val(IC), .valout(sr_bit_1_valout));  // open: nvalout
  nor nor_1 (nor_1_out, not_3_out, not_20_out);
  sr_bit sr_bit_2 (.clk1(clk1), .clk2(clk2), .val(sr_bit_1_valout), .valout(sr_bit_2_valout));  // open: nvalout
  sr_bit sr_bit_3 (.clk1(clk1), .clk2(clk2), .val(nor_1_out), .valout(sr_bit_3_valout));  // open: nvalout
  sr_bit sr_bit_4 (.clk1(clk1), .clk2(clk2), .val(sr_bit_2_valout), .valout(sr_bit_4_valout));  // open: nvalout
  not not_1 (not_1_out, sr_bit_1_valout);
  sr_bit sr_bit_5 (.clk1(clk1), .clk2(clk2), .val(sr_bit_3_valout), .valout(sr_bit_5_valout));  // open: nvalout
  sr_bit sr_bit_6 (.clk1(clk1), .clk2(clk2), .val(sr_bit_4_valout), .valout(sr_bit_6_valout));  // open: nvalout
  sr_bit sr_bit_7 (.clk1(clk1), .clk2(clk2), .val(sr_bit_6_valout), .valout(sr_bit_7_valout));  // open: nvalout
  nor nor_2 (nor_2_out, sr_bit_42_valout, not_1_out);
  not not_2 (not_2_out, nor_2_out);
  sr_bit sr_bit_8 (.clk1(clk1), .clk2(clk2), .val(sr_bit_5_valout), .valout(sr_bit_8_valout));  // open: nvalout
  sr_bit sr_bit_9 (.clk1(clk1), .clk2(clk2), .val(sr_bit_8_valout), .valout(sr_bit_9_valout));  // open: nvalout
  sr_bit sr_bit_10 (.clk1(clk1), .clk2(clk2), .val(sr_bit_7_valout), .valout(sr_bit_10_valout));  // open: nvalout
  sr_bit sr_bit_11 (.clk1(clk1), .clk2(clk2), .val(not_2_out), .valout(sr_bit_11_valout));  // open: nvalout
  sr_bit sr_bit_12 (.clk1(clk1), .clk2(clk2), .val(sr_bit_9_valout), .valout(sr_bit_12_valout));  // open: nvalout
  sr_bit sr_bit_13 (.clk1(clk1), .clk2(clk2), .val(sr_bit_10_valout), .valout(sr_bit_13_valout));  // open: nvalout
  sr_bit sr_bit_14 (.clk1(clk1), .clk2(clk2), .val(sr_bit_11_valout), .valout(sr_bit_14_valout));  // open: nvalout
  sr_bit sr_bit_15 (.clk1(clk1), .clk2(clk2), .val(sr_bit_12_valout), .valout(sr_bit_15_valout));  // open: nvalout
  sr_bit sr_bit_16 (.clk1(clk1), .clk2(clk2), .val(sr_bit_13_valout), .valout(sr_bit_16_valout));  // open: nvalout
  not not_3 (not_3_out, not_2_out);
  sr_bit sr_bit_17 (.clk1(clk1), .clk2(clk2), .val(sr_bit_14_valout), .valout(sr_bit_17_valout));  // open: nvalout
  sr_bit sr_bit_18 (.clk1(clk1), .clk2(clk2), .val(sr_bit_16_valout), .valout(sr_bit_18_valout));  // open: nvalout
  not not_4 (res_latch2, sr_bit_17_valout);
  sr_bit sr_bit_19 (.clk1(clk1), .clk2(clk2), .val(sr_bit_15_valout), .valout(sr_bit_19_valout));  // open: nvalout
  sr_bit sr_bit_20 (.clk1(clk1), .clk2(clk2), .val(sr_bit_18_valout), .valout(sr_bit_20_valout));  // open: nvalout
  sr_bit sr_bit_21 (.clk1(clk1), .clk2(clk2), .val(sr_bit_17_valout), .valout(sr_bit_21_valout));  // open: nvalout
  sr_bit sr_bit_22 (.clk1(clk1), .clk2(clk2), .val(sr_bit_19_valout), .valout(sr_bit_22_valout));  // open: nvalout
  sr_bit sr_bit_23 (.clk1(clk1), .clk2(clk2), .val(sr_bit_20_valout), .valout(sr_bit_23_valout));  // open: nvalout
  not not_5 (res_latch1, sr_bit_21_valout);
  sr_bit sr_bit_24 (.clk1(clk1), .clk2(clk2), .val(sr_bit_22_valout), .valout(sr_bit_24_valout));  // open: nvalout
  sr_bit sr_bit_25 (.clk1(clk1), .clk2(clk2), .val(sr_bit_23_valout), .valout(sr_bit_25_valout));  // open: nvalout
  sr_bit sr_bit_26 (.clk1(clk1), .clk2(clk2), .val(sr_bit_24_valout), .valout(sr_bit_26_valout));  // open: nvalout
  sr_bit sr_bit_27 (.clk1(clk1), .clk2(clk2), .val(sr_bit_25_valout), .valout(sr_bit_27_valout));  // open: nvalout
  sr_bit sr_bit_28 (.clk1(clk1), .clk2(clk2), .val(sr_bit_26_valout), .valout(sr_bit_28_valout));  // open: nvalout
  sr_bit sr_bit_29 (.clk1(clk1), .clk2(clk2), .val(sr_bit_27_valout), .valout(sr_bit_29_valout));  // open: nvalout
  sr_bit sr_bit_30 (.clk1(clk1), .clk2(clk2), .val(sr_bit_28_valout), .valout(sr_bit_30_valout));  // open: nvalout
  sr_bit sr_bit_31 (.clk1(clk1), .clk2(clk2), .val(sr_bit_29_valout), .valout(sr_bit_31_valout));  // open: nvalout
  sr_bit sr_bit_32 (.clk1(clk1), .clk2(clk2), .val(sr_bit_31_valout), .valout(sr_bit_32_valout));  // open: nvalout
  nor nor_3 (nor_3_out, sr_bit_3_valout, sr_bit_8_valout, sr_bit_12_valout, sr_bit_19_valout, sr_bit_24_valout, sr_bit_28_valout);
  not not_6 (not_6_out, nor_4_out);
  nor nor_4 (nor_4_out, sr_bit_8_valout, sr_bit_9_valout, sr_bit_12_valout, sr_bit_15_valout, sr_bit_19_valout, sr_bit_22_valout, sr_bit_24_valout, sr_bit_26_valout, sr_bit_28_valout, sr_bit_30_valout);
  nor nor_5 (nor_5_out, sr_bit_8_valout, sr_bit_9_valout, sr_bit_24_valout, sr_bit_26_valout);
  nor nor_6 (nor_6_out, sr_bit_3_valout, sr_bit_15_valout, sr_bit_19_valout, sr_bit_30_valout);
  nor nor_7 (nor_7_out, sr_bit_24_valout, sr_bit_26_valout, sr_bit_28_valout, sr_bit_30_valout);
  nor nor_8 (nor_8_out, sr_bit_3_valout, sr_bit_5_valout, sr_bit_8_valout, sr_bit_9_valout, sr_bit_12_valout, sr_bit_15_valout, sr_bit_19_valout, sr_bit_22_valout, sr_bit_24_valout, sr_bit_26_valout, sr_bit_28_valout);
  nor nor_9 (nor_9_out, sr_bit_3_valout, sr_bit_9_valout, sr_bit_19_valout, sr_bit_26_valout);
  nor nor_10 (nor_10_out, sr_bit_8_valout, sr_bit_9_valout, sr_bit_12_valout, sr_bit_15_valout);
  nor nor_11 (nor_11_out, sr_bit_8_valout, sr_bit_15_valout, sr_bit_24_valout, sr_bit_30_valout);
  sr_bit sr_bit_33 (.clk1(clk1), .clk2(clk2), .val(sr_bit_32_valout), .valout(sr_bit_33_valout));  // open: nvalout
  sr_bit sr_bit_34 (.clk1(clk1), .clk2(clk2), .val(nor_3_out), .valout(sr_bit_34_valout));  // open: nvalout
  D_Flip_Flop #(.trigger("high")) d_ff_1 (.D(not_6_out), .clk(clk1), .Qn(out_14));  // open: Q, preset, reset
  sr_bit sr_bit_35 (.clk1(clk1), .clk2(clk2), .val(nor_5_out), .valout(sr_bit_35_valout));  // open: nvalout
  sr_bit sr_bit_36 (.clk1(clk1), .clk2(clk2), .val(nor_6_out), .valout(sr_bit_36_valout));  // open: nvalout
  sr_bit sr_bit_37 (.clk1(clk1), .clk2(clk2), .val(nor_7_out), .valout(sr_bit_37_valout));  // open: nvalout
  sr_bit sr_bit_38 (.clk1(clk1), .clk2(clk2), .val(nor_9_out), .valout(sr_bit_38_valout));  // open: nvalout
  sr_bit sr_bit_39 (.clk1(clk1), .clk2(clk2), .val(nor_10_out), .valout(sr_bit_39_valout));  // open: nvalout
  sr_bit sr_bit_40 (.clk1(clk1), .clk2(clk2), .val(nor_11_out), .valout(sr_bit_40_valout));  // open: nvalout
  sr_bit sr_bit_41 (.clk1(clk1), .clk2(clk2), .val(sr_bit_33_valout), .valout(sr_bit_41_valout));  // open: nvalout
  not not_7 (out_12, sr_bit_37_valout);
  not not_8 (out_13, sr_bit_39_valout);
  sr_bit sr_bit_42 (.clk1(clk1), .clk2(clk2), .val(sr_bit_41_valout), .valout(sr_bit_42_valout));  // open: nvalout
  not not_9 (not_9_out, sr_bit_34_valout);
  nor nor_12 (out_8, sr_bit_34_valout, not_15_out);
  nor nor_13 (out_9, not_9_out, not_13_out);
  nor nor_14 (out_10, sr_bit_38_valout, not_19_out);
  nor nor_15 (out_11, sr_bit_40_valout, not_17_out);
  not not_10 (fm_clk2, sr_bit_35_valout);
  not not_11 (fm_clk1, sr_bit_36_valout);
  not not_12 (not_12_out, out_8);
  not not_13 (not_13_out, not_12_out);
  not not_14 (not_14_out, out_9);
  not not_15 (not_15_out, not_14_out);
  not not_16 (not_16_out, out_10);
  not not_17 (not_17_out, not_16_out);
  not not_18 (not_18_out, out_11);
  not not_19 (not_19_out, not_18_out);
  not not_20 (not_20_out, nor_8_out);
endmodule

module clk_div_2612 (
  input  clk1,
  input  clk2,
  input  IC,
  output fm_clk1,
  output fm_clk2,
  output res_latch1
);

  wire nor_1_out, nor_2_out, nor_3_out, nor_4_out, nor_5_out, not_1_out, not_2_out, not_3_out, not_5_out,
       sr_bit_1_valout, sr_bit_2_valout, sr_bit_3_valout, sr_bit_4_valout, sr_bit_5_valout, sr_bit_6_valout,
       sr_bit_7_valout, sr_bit_8_valout, sr_bit_9_valout, sr_bit_10_valout, sr_bit_11_valout,
       sr_bit_12_valout, sr_bit_13_valout, sr_bit_14_valout, sr_bit_15_valout, sr_bit_16_valout,
       sr_bit_17_valout, sr_bit_18_valout, sr_bit_19_valout, sr_bit_20_valout, sr_bit_21_valout,
       sr_bit_22_valout, sr_bit_23_valout, sr_bit_24_valout;

  nor nor_1 (nor_1_out, not_3_out, not_5_out);
  sr_bit sr_bit_1 (.clk1(clk1), .clk2(clk2), .val(IC), .valout(sr_bit_1_valout));  // open: nvalout
  sr_bit sr_bit_2 (.clk1(clk1), .clk2(clk2), .val(nor_1_out), .valout(sr_bit_2_valout));  // open: nvalout
  sr_bit sr_bit_3 (.clk1(clk1), .clk2(clk2), .val(sr_bit_1_valout), .valout(sr_bit_3_valout));  // open: nvalout
  not not_1 (not_1_out, IC);
  sr_bit sr_bit_4 (.clk1(clk1), .clk2(clk2), .val(sr_bit_2_valout), .valout(sr_bit_4_valout));  // open: nvalout
  sr_bit sr_bit_5 (.clk1(clk1), .clk2(clk2), .val(sr_bit_3_valout), .valout(sr_bit_5_valout));  // open: nvalout
  sr_bit sr_bit_6 (.clk1(clk1), .clk2(clk2), .val(sr_bit_5_valout), .valout(sr_bit_6_valout));  // open: nvalout
  nor nor_2 (nor_2_out, sr_bit_24_valout, not_1_out);
  not not_2 (not_2_out, nor_2_out);
  sr_bit sr_bit_7 (.clk1(clk1), .clk2(clk2), .val(sr_bit_4_valout), .valout(sr_bit_7_valout));  // open: nvalout
  sr_bit sr_bit_8 (.clk1(clk1), .clk2(clk2), .val(sr_bit_7_valout), .valout(sr_bit_8_valout));  // open: nvalout
  sr_bit sr_bit_9 (.clk1(clk1), .clk2(clk2), .val(sr_bit_6_valout), .valout(sr_bit_9_valout));  // open: nvalout
  sr_bit sr_bit_10 (.clk1(clk1), .clk2(clk2), .val(not_2_out), .valout(sr_bit_10_valout));  // open: nvalout
  sr_bit sr_bit_11 (.clk1(clk1), .clk2(clk2), .val(sr_bit_8_valout), .valout(sr_bit_11_valout));  // open: nvalout
  sr_bit sr_bit_12 (.clk1(clk1), .clk2(clk2), .val(sr_bit_9_valout), .valout(sr_bit_12_valout));  // open: nvalout
  sr_bit sr_bit_13 (.clk1(clk1), .clk2(clk2), .val(sr_bit_10_valout), .valout(sr_bit_13_valout));  // open: nvalout
  sr_bit sr_bit_14 (.clk1(clk1), .clk2(clk2), .val(sr_bit_11_valout), .valout(sr_bit_14_valout));  // open: nvalout
  sr_bit sr_bit_15 (.clk1(clk1), .clk2(clk2), .val(sr_bit_12_valout), .valout(sr_bit_15_valout));  // open: nvalout
  not not_3 (not_3_out, not_2_out);
  sr_bit sr_bit_16 (.clk1(clk1), .clk2(clk2), .val(sr_bit_13_valout), .valout(sr_bit_16_valout));  // open: nvalout
  sr_bit sr_bit_17 (.clk1(clk1), .clk2(clk2), .val(sr_bit_15_valout), .valout(sr_bit_17_valout));  // open: nvalout
  nor nor_3 (nor_3_out, sr_bit_7_valout, sr_bit_8_valout);
  nor nor_4 (nor_4_out, sr_bit_2_valout, sr_bit_14_valout);
  sr_bit sr_bit_18 (.clk1(clk1), .clk2(clk2), .val(sr_bit_17_valout), .valout(sr_bit_18_valout));  // open: nvalout
  sr_bit sr_bit_19 (.clk1(clk1), .clk2(clk2), .val(sr_bit_16_valout), .valout(sr_bit_19_valout));  // open: nvalout
  nor nor_5 (nor_5_out, sr_bit_2_valout, sr_bit_4_valout, sr_bit_7_valout, sr_bit_8_valout, sr_bit_11_valout);
  sr_bit sr_bit_20 (.clk1(clk1), .clk2(clk2), .val(sr_bit_18_valout), .valout(sr_bit_20_valout));  // open: nvalout
  not not_4 (res_latch1, sr_bit_19_valout);
  sr_bit sr_bit_21 (.clk1(clk1), .clk2(clk2), .val(nor_3_out), .valout(sr_bit_21_valout));  // open: nvalout
  sr_bit sr_bit_22 (.clk1(clk1), .clk2(clk2), .val(nor_4_out), .valout(sr_bit_22_valout));  // open: nvalout
  not not_5 (not_5_out, nor_5_out);
  sr_bit sr_bit_23 (.clk1(clk1), .clk2(clk2), .val(sr_bit_20_valout), .valout(sr_bit_23_valout));  // open: nvalout
  sr_bit sr_bit_24 (.clk1(clk1), .clk2(clk2), .val(sr_bit_23_valout), .valout(sr_bit_24_valout));  // open: nvalout
  not not_6 (fm_clk2, sr_bit_21_valout);
  not not_7 (fm_clk1, sr_bit_22_valout);
endmodule

module ym2612 (
  input  in_1,
  output out_2,
  output out_3
);

  wire clk_gen_1_clk1, clk_gen_1_clk2, clock_1_out, controlled_buffer_1_out, undriven;
  wire [8:0] write_data_1_valout;

  Clock clock_1 (.out(clock_1_out));
  clk_gen clk_gen_1 (.MCLK(clock_1_out), .clk1(clk_gen_1_clk1), .clk2(clk_gen_1_clk2));
  clk_div_2612 clk_div_2612_1 (
    .clk1(clk_gen_1_clk1), .clk2(clk_gen_1_clk2), .IC(in_1), .fm_clk1(out_2), .fm_clk2(out_3));  // open: res_latch1
  write_data write_data_1 (.valout(write_data_1_valout));  // open: data_in, bank, write, oe, nvalout
  assign controlled_buffer_1_out = undriven ? write_data_1_valout[0] : 1'bz;  // Controlled_Buffer controlled_buffer_1
  assign controlled_buffer_1_out = undriven ? write_data_1_valout[1] : 1'bz;  // Controlled_Buffer controlled_buffer_2
  assign controlled_buffer_1_out = undriven ? write_data_1_valout[2] : 1'bz;  // Controlled_Buffer controlled_buffer_3
  assign controlled_buffer_1_out = undriven ? write_data_1_valout[3] : 1'bz;  // Controlled_Buffer controlled_buffer_4
  assign controlled_buffer_1_out = undriven ? write_data_1_valout[4] : 1'bz;  // Controlled_Buffer controlled_buffer_5
  assign controlled_buffer_1_out = undriven ? write_data_1_valout[5] : 1'bz;  // Controlled_Buffer controlled_buffer_6
  assign controlled_buffer_1_out = undriven ? write_data_1_valout[6] : 1'bz;  // Controlled_Buffer controlled_buffer_7
  assign controlled_buffer_1_out = undriven ? write_data_1_valout[7] : 1'bz;  // Controlled_Buffer controlled_buffer_8
  // also tied to GND on the sheet: controlled_buffer_1_out
endmodule

module reg_glob (
  input  clk1,
  input  clk2,
  input  [8:0] write_data,
  input  [8:0] write_data_neg,
  input  addr_wr,
  input  data_wr,
  input  IC,
  output busy,
  output op_reg_bank_sel,
  output keyon,
  output keyon_csm,
  output timer_a_status
);

  wire and_1_out, and_2_out, and_3_out, and_4_out, and_5_out, and_6_out, and_7_out, and_8_out, and_9_out,
       and_10_out, and_11_out, and_12_out, and_13_out, and_14_out, and_15_out, and_16_out, and_17_out,
       and_18_out, and_19_out, and_20_out, and_21_out, cnt_bit_1_cout, cnt_bit_2_cout, cnt_bit_2_valout,
       cnt_bit_3_cout, cnt_bit_4_valout, cnt_bit_5_cout, cnt_bit_6_cout, cnt_bit_6_valout, cnt_bit_7_cout,
       cnt_bit_8_cout, cnt_bit_8_valout, cnt_bit_9_cout, controlled_buffer_1_out, controlled_buffer_3_out,
       controlled_buffer_5_out, d_ff_1_qn, d_ff_2_q, d_ff_3_qn, d_ff_4_qn, d_ff_5_qn, d_ff_6_qn, d_ff_7_qn,
       d_ff_8_qn, d_ff_9_qn, d_ff_10_qn, d_ff_11_qn, d_ff_12_qn, d_ff_13_qn, d_ff_14_qn, d_ff_15_qn,
       d_ff_16_qn, d_ff_17_qn, d_ff_18_q, d_ff_18_qn, d_ff_19_qn, d_ff_20_qn, d_ff_21_qn, d_ff_22_q,
       d_ff_23_q, d_ff_24_qn, d_ff_25_q, d_ff_26_qn, d_ff_27_qn, d_ff_28_q, d_ff_29_qn, d_ff_30_q, d_ff_31_q,
       d_ff_33_q, nand_1_out, nand_2_out, nand_3_out, nor_1_out, nor_2_out, nor_3_out, nor_4_out, nor_5_out,
       nor_6_out, nor_7_out, nor_8_out, nor_9_out, nor_10_out, nor_11_out, nor_12_out, nor_13_out,
       nor_14_out, nor_15_out, nor_16_out, nor_17_out, nor_18_out, nor_19_out, nor_20_out, nor_21_out,
       nor_22_out, nor_23_out, nor_24_out, nor_25_out, nor_26_out, nor_27_out, nor_28_out, nor_29_out,
       nor_30_out, nor_31_out, nor_32_out, nor_33_out, nor_34_out, nor_35_out, nor_36_out, nor_37_out,
       nor_38_out, nor_39_out, nor_40_out, nor_41_out, nor_42_out, nor_43_out, nor_44_out, nor_45_out,
       nor_46_out, nor_47_out, nor_48_out, nor_49_out, nor_50_out, nor_51_out, nor_52_out, nor_53_out,
       nor_54_out, nor_55_out, nor_56_out, nor_57_out, nor_58_out, not_1_out, not_2_out, not_3_out,
       not_4_out, not_5_out, not_6_out, not_7_out, not_8_out, not_9_out, not_10_out, not_11_out, not_12_out,
       not_13_out, not_14_out, not_15_out, not_17_out, not_18_out, not_20_out, not_21_out, not_22_out,
       not_23_out, not_24_out, not_25_out, or_1_out, or_2_out, or_3_out, or_4_out, reg_bit_2_10_valout,
       reg_bit_2_11_valout, reg_bit_2_12_valout, reg_bit_4_41_valout, reg_bit_4_42_valout,
       reg_bit_4_43_valout, reg_bit_4_44_valout, sr_bit_1_nvalout, sr_bit_1_valout, sr_bit_2_nvalout,
       sr_bit_2_valout, sr_bit_3_nvalout, sr_bit_3_valout, sr_bit_4_nvalout, sr_bit_4_valout,
       sr_bit_5_nvalout, sr_bit_5_valout, sr_bit_6_nvalout, sr_bit_6_valout, sr_bit_7_nvalout,
       sr_bit_7_valout, sr_bit_8_nvalout, sr_bit_8_valout, sr_bit_9_nvalout, sr_bit_9_valout,
       sr_bit_10_nvalout, sr_bit_10_valout, sr_bit_11_valout, sr_bit_12_valout, sr_bit_13_valout,
       sr_bit_14_valout, sr_bit_15_valout, sr_bit_16_valout, sr_bit_17_valout, sr_bit_18_valout,
       sr_bit_19_valout, sr_bit_20_valout, sr_bit_21_valout, sr_bit_22_valout, sr_bit_23_valout,
       sr_bit_24_valout, sr_bit_25_valout, sr_bit_26_valout, sr_bit_27_valout, sr_bit_28_valout,
       sr_bit_29_nvalout, sr_bit_30_valout, sr_bit_31_valout, sr_bit_32_valout, sr_bit_33_valout,
       sr_bit_34_valout, sr_bit_35_valout, sr_bit_36_valout, sr_bit_37_nvalout, timer_bit_1_out_7,
       timer_bit_2_out_7, timer_bit_3_out_7, timer_bit_4_out_7, timer_bit_5_out_7, timer_bit_6_out_7,
       timer_bit_7_out_7, timer_bit_8_out_7, timer_bit_9_out_7, timer_bit_10_out_7, undriven, undriven_2,
       undriven_3, undriven_4, undriven_5, undriven_7, undriven_8, undriven_9, undriven_10, undriven_11;
  wire [8:0] not_16_out, reg_bit_2_1_valout;
  wire [9:0] undriven_6;

  D_Flip_Flop #(.trigger("high")) d_ff_1 (.D(IC), .clk(clk1), .Qn(d_ff_1_qn));  // open: Q, preset, reset
  nor nor_1 (nor_1_out, write_data[4], write_data[5], write_data[6], write_data[7]);
  nor nor_2 (nor_2_out, write_data[8], write_data[7], write_data[6], write_data[5], write_data_neg[4], write_data_neg[3], write_data_neg[2], write_data[1], write_data[0], addr_wr);
  nor nor_3 (nor_3_out, write_data[8], write_data[7], write_data[6], write_data_neg[5], write_data[4], write_data[3], write_data_neg[2], write_data_neg[1], write_data_neg[0], addr_wr);
  nor nor_4 (nor_4_out, write_data[8], write_data[7], write_data[6], write_data_neg[5], write_data[4], write_data[3], write_data_neg[2], write_data[1], write_data_neg[0], addr_wr);
  nor nor_5 (nor_5_out, write_data[8], write_data[7], write_data[6], write_data_neg[5], write_data[4], write_data[3], write_data_neg[2], write_data[1], write_data[0], addr_wr);
  not not_1 (not_1_out, write_data[8]);
  nor nor_6 (nor_6_out, not_1_out, write_data[7], write_data[6], write_data[5], write_data[4], write_data[3], write_data[2], write_data_neg[1], write_data[0], addr_wr);
  nor nor_7 (nor_7_out, write_data[8], write_data[7], write_data[6], write_data_neg[5], write_data[4], write_data[3], write_data[2], write_data_neg[1], write_data[0], addr_wr);
  nor nor_8 (nor_8_out, write_data[8], write_data[7], write_data[6], write_data_neg[5], write_data[4], write_data[3], write_data_neg[2], write_data_neg[1], write_data[0], addr_wr);
  nor nor_9 (nor_9_out, write_data[8], write_data[7], write_data[6], write_data_neg[5], write_data[4], write_data_neg[3], write_data[2], write_data[1], write_data[0], addr_wr);
  nor nor_10 (nor_10_out, write_data[8], write_data[7], write_data[6], write_data_neg[5], write_data[4], write_data[3], write_data[2], write_data[1], write_data_neg[0], addr_wr);
  nor nor_11 (nor_11_out, nor_1_out, addr_wr);
  and and_1 (and_1_out, addr_wr, sr_bit_1_nvalout);
  and and_2 (and_2_out, addr_wr, sr_bit_2_nvalout);
  and and_3 (and_3_out, addr_wr, sr_bit_3_nvalout);
  and and_4 (and_4_out, addr_wr, sr_bit_4_nvalout);
  and and_5 (and_5_out, addr_wr, sr_bit_5_nvalout);
  and and_6 (and_6_out, addr_wr, d_ff_3_qn);
  and and_7 (and_7_out, addr_wr, sr_bit_6_nvalout);
  and and_8 (and_8_out, addr_wr, sr_bit_7_nvalout);
  and and_9 (and_9_out, addr_wr, sr_bit_8_nvalout);
  and and_10 (and_10_out, addr_wr, sr_bit_9_nvalout);
  and and_11 (and_11_out, addr_wr, sr_bit_10_nvalout);
  nor nor_12 (nor_12_out, nor_11_out, and_1_out);
  nor nor_13 (nor_13_out, nor_2_out, and_2_out);
  nor nor_14 (nor_14_out, nor_3_out, and_3_out);
  nor nor_15 (nor_15_out, nor_4_out, and_4_out);
  nor nor_16 (nor_16_out, nor_5_out, and_5_out);
  nor nor_17 (nor_17_out, nor_27_out, and_6_out);
  nor nor_18 (nor_18_out, nor_6_out, and_7_out);
  nor nor_19 (nor_19_out, nor_7_out, and_8_out);
  nor nor_20 (nor_20_out, nor_8_out, and_9_out);
  nor nor_21 (nor_21_out, nor_9_out, and_10_out);
  nor nor_22 (nor_22_out, nor_10_out, and_11_out);
  sr_bit sr_bit_1 (.clk1(clk1), .clk2(clk2), .val(nor_12_out), .nvalout(sr_bit_1_nvalout), .valout(sr_bit_1_valout));
  sr_bit sr_bit_2 (.clk1(clk1), .clk2(clk2), .val(nor_13_out), .nvalout(sr_bit_2_nvalout), .valout(sr_bit_2_valout));
  sr_bit sr_bit_3 (.clk1(clk1), .clk2(clk2), .val(nor_14_out), .nvalout(sr_bit_3_nvalout), .valout(sr_bit_3_valout));
  sr_bit sr_bit_4 (.clk1(clk1), .clk2(clk2), .val(nor_15_out), .nvalout(sr_bit_4_nvalout), .valout(sr_bit_4_valout));
  sr_bit sr_bit_5 (.clk1(clk1), .clk2(clk2), .val(nor_16_out), .nvalout(sr_bit_5_nvalout), .valout(sr_bit_5_valout));
  D_Flip_Flop #(.trigger("high")) d_ff_2 (.D(nor_17_out), .clk(clk1), .Q(d_ff_2_q));  // open: Qn, preset, reset
  sr_bit sr_bit_6 (.clk1(clk1), .clk2(clk2), .val(nor_18_out), .nvalout(sr_bit_6_nvalout), .valout(sr_bit_6_valout));
  sr_bit sr_bit_7 (.clk1(clk1), .clk2(clk2), .val(nor_19_out), .nvalout(sr_bit_7_nvalout), .valout(sr_bit_7_valout));
  sr_bit sr_bit_8 (.clk1(clk1), .clk2(clk2), .val(nor_20_out), .nvalout(sr_bit_8_nvalout), .valout(sr_bit_8_valout));
  sr_bit sr_bit_9 (.clk1(clk1), .clk2(clk2), .val(nor_21_out), .nvalout(sr_bit_9_nvalout), .valout(sr_bit_9_valout));
  sr_bit sr_bit_10 (.clk1(clk1), .clk2(clk2), .val(nor_22_out), .nvalout(sr_bit_10_nvalout), .valout(sr_bit_10_valout));
  D_Flip_Flop #(.trigger("high")) d_ff_3 (.D(d_ff_2_q), .clk(clk2), .Qn(d_ff_3_qn));  // open: Q, preset, reset
  nor nor_23 (nor_23_out, sr_bit_2_valout, write_data[8], data_wr);
  nor nor_24 (nor_24_out, sr_bit_3_valout, write_data[8], data_wr);
  nor nor_25 (nor_25_out, sr_bit_4_valout, write_data[8], data_wr);
  nor nor_26 (nor_26_out, sr_bit_5_valout, write_data[8], data_wr);
  nor nor_27 (nor_27_out, sr_bit_1_valout, data_wr);
  nor nor_28 (nor_28_out, sr_bit_6_valout, not_1_out, data_wr);
  nor nor_29 (nor_29_out, sr_bit_7_valout, write_data[8], data_wr);
  nor nor_30 (nor_30_out, sr_bit_8_valout, write_data[8], data_wr);
  nor nor_31 (nor_31_out, sr_bit_9_valout, write_data[8], data_wr);
  nor nor_32 (nor_32_out, sr_bit_10_valout, write_data[8], data_wr);
  not not_2 (not_2_out, nor_11_out);
  not not_3 (not_3_out, nor_23_out);
  not not_4 (not_4_out, nor_24_out);
  not not_5 (not_5_out, nor_25_out);
  not not_6 (not_6_out, nor_26_out);
  nand nand_1 (nand_1_out, nor_24_out, write_data[4]);
  nand nand_2 (nand_2_out, nor_24_out, write_data[5]);
  sr_bit sr_bit_11 (.clk1(clk1), .clk2(clk2), .val(nand_1_out), .valout(sr_bit_11_valout));  // open: nvalout
  sr_bit sr_bit_12 (.clk1(clk1), .clk2(clk2), .val(nand_2_out), .valout(sr_bit_12_valout));  // open: nvalout
  reg_bit_2 reg_bit_2_1 (
    .clk1(clk1), .clk2(clk2), .val(write_data[0]), .load(nor_11_out), .nload(not_2_out), .ic(d_ff_1_qn),
    .valout(reg_bit_2_1_valout[0]));
  reg_bit_2 reg_bit_2_2 (
    .clk1(clk1), .clk2(clk2), .val(write_data[1]), .load(nor_11_out), .nload(not_2_out), .ic(d_ff_1_qn),
    .valout(reg_bit_2_1_valout[1]));
  reg_bit_2 reg_bit_2_3 (
    .clk1(clk1), .clk2(clk2), .val(write_data[2]), .load(nor_11_out), .nload(not_2_out), .ic(d_ff_1_qn),
    .valout(reg_bit_2_1_valout[2]));
  reg_bit_2 reg_bit_2_4 (
    .clk1(clk1), .clk2(clk2), .val(write_data[3]), .load(nor_11_out), .nload(not_2_out), .ic(d_ff_1_qn),
    .valout(reg_bit_2_1_valout[3]));
  reg_bit_2 reg_bit_2_5 (
    .clk1(clk1), .clk2(clk2), .val(write_data[4]), .load(nor_11_out), .nload(not_2_out), .ic(d_ff_1_qn),
    .valout(reg_bit_2_1_valout[4]));
  reg_bit_2 reg_bit_2_6 (
    .clk1(clk1), .clk2(clk2), .val(write_data[5]), .load(nor_11_out), .nload(not_2_out), .ic(d_ff_1_qn),
    .valout(reg_bit_2_1_valout[5]));
  reg_bit_2 reg_bit_2_7 (
    .clk1(clk1), .clk2(clk2), .val(write_data[6]), .load(nor_11_out), .nload(not_2_out), .ic(d_ff_1_qn),
    .valout(reg_bit_2_1_valout[6]));
  reg_bit_2 reg_bit_2_8 (
    .clk1(clk1), .clk2(clk2), .val(write_data[7]), .load(nor_11_out), .nload(not_2_out), .ic(d_ff_1_qn),
    .valout(reg_bit_2_1_valout[7]));
  reg_bit_2 reg_bit_2_9 (
    .clk1(clk1), .clk2(clk2), .val(write_data[8]), .load(nor_11_out), .nload(not_2_out), .ic(d_ff_1_qn),
    .valout(reg_bit_2_1_valout[8]));
  reg_bit_3 reg_bit_3_1 (
    .clk1(clk1), .clk2(clk2), .val(write_data[0]), .load(nor_23_out), .nload(not_3_out), .ic(d_ff_1_qn));  // open: valout
  reg_bit_3 reg_bit_3_2 (
    .clk1(clk1), .clk2(clk2), .val(write_data[1]), .load(nor_23_out), .nload(not_3_out), .ic(d_ff_1_qn));  // open: valout
  reg_bit_3 reg_bit_3_3 (
    .clk1(clk1), .clk2(clk2), .val(write_data[2]), .load(nor_23_out), .nload(not_3_out), .ic(d_ff_1_qn));  // open: valout
  reg_bit_3 reg_bit_3_4 (
    .clk1(clk1), .clk2(clk2), .val(write_data[3]), .load(nor_23_out), .nload(not_3_out), .ic(d_ff_1_qn));  // open: valout
  reg_bit_3 reg_bit_3_5 (
    .clk1(clk1), .clk2(clk2), .val(write_data[4]), .load(nor_23_out), .nload(not_3_out), .ic(d_ff_1_qn));  // open: valout
  reg_bit_3 reg_bit_3_6 (
    .clk1(clk1), .clk2(clk2), .val(write_data[5]), .load(nor_23_out), .nload(not_3_out), .ic(d_ff_1_qn));  // open: valout
  reg_bit_3 reg_bit_3_7 (
    .clk1(clk1), .clk2(clk2), .val(write_data[7]), .load(nor_23_out), .nload(not_3_out), .ic(d_ff_1_qn));  // open: valout
  reg_bit_4 reg_bit_4_1 (
    .clk1(clk1), .clk2(clk2), .val(write_data[0]), .load(nor_24_out), .nload(not_4_out), .ic(d_ff_1_qn));  // open: valout
  reg_bit_4 reg_bit_4_2 (
    .clk1(clk1), .clk2(clk2), .val(write_data[1]), .load(nor_24_out), .nload(not_4_out), .ic(d_ff_1_qn));  // open: valout
  reg_bit_4 reg_bit_4_3 (
    .clk1(clk1), .clk2(clk2), .val(write_data[2]), .load(nor_24_out), .nload(not_4_out), .ic(d_ff_1_qn));  // open: valout
  reg_bit_4 reg_bit_4_4 (
    .clk1(clk1), .clk2(clk2), .val(write_data[3]), .load(nor_24_out), .nload(not_4_out), .ic(d_ff_1_qn));  // open: valout
  reg_bit_4 reg_bit_4_5 (
    .clk1(clk1), .clk2(clk2), .val(write_data[6]), .load(nor_24_out), .nload(not_4_out), .ic(d_ff_1_qn));  // open: valout
  reg_bit_4 reg_bit_4_6 (
    .clk1(clk1), .clk2(clk2), .val(write_data[7]), .load(nor_24_out), .nload(not_4_out), .ic(d_ff_1_qn));  // open: valout
  reg_bit_4 reg_bit_4_7 (
    .clk1(clk1), .clk2(clk2), .val(write_data[0]), .load(nor_25_out), .nload(not_5_out), .ic(d_ff_1_qn));  // open: valout
  reg_bit_4 reg_bit_4_8 (
    .clk1(clk1), .clk2(clk2), .val(write_data[1]), .load(nor_25_out), .nload(not_5_out), .ic(d_ff_1_qn));  // open: valout
  reg_bit_4 reg_bit_4_9 (
    .clk1(clk1), .clk2(clk2), .val(write_data[0]), .load(nor_26_out), .nload(not_6_out), .ic(d_ff_1_qn));  // open: valout
  reg_bit_4 reg_bit_4_10 (
    .clk1(clk1), .clk2(clk2), .val(write_data[1]), .load(nor_26_out), .nload(not_6_out), .ic(d_ff_1_qn));  // open: valout
  reg_bit_4 reg_bit_4_11 (
    .clk1(clk1), .clk2(clk2), .val(write_data[2]), .load(nor_26_out), .nload(not_6_out), .ic(d_ff_1_qn));  // open: valout
  reg_bit_4 reg_bit_4_12 (
    .clk1(clk1), .clk2(clk2), .val(write_data[3]), .load(nor_26_out), .nload(not_6_out), .ic(d_ff_1_qn));  // open: valout
  reg_bit_4 reg_bit_4_13 (
    .clk1(clk1), .clk2(clk2), .val(write_data[4]), .load(nor_26_out), .nload(not_6_out), .ic(d_ff_1_qn));  // open: valout
  reg_bit_4 reg_bit_4_14 (
    .clk1(clk1), .clk2(clk2), .val(write_data[5]), .load(nor_26_out), .nload(not_6_out), .ic(d_ff_1_qn));  // open: valout
  reg_bit_4 reg_bit_4_15 (
    .clk1(clk1), .clk2(clk2), .val(write_data[6]), .load(nor_26_out), .nload(not_6_out), .ic(d_ff_1_qn));  // open: valout
  reg_bit_4 reg_bit_4_16 (
    .clk1(clk1), .clk2(clk2), .val(write_data[7]), .load(nor_26_out), .nload(not_6_out), .ic(d_ff_1_qn));  // open: valout
  not not_7 (not_7_out, nor_27_out);
  not not_8 (not_8_out, nor_28_out);
  not not_9 (not_9_out, nor_29_out);
  not not_10 (not_10_out, nor_30_out);
  not not_11 (not_11_out, nor_31_out);
  not not_12 (not_12_out, nor_32_out);
  reg_bit_4 reg_bit_4_17 (
    .clk1(clk1), .clk2(clk2), .val(write_data[0]), .load(nor_27_out), .nload(not_7_out), .ic(d_ff_1_qn));  // open: valout
  reg_bit_4 reg_bit_4_18 (
    .clk1(clk1), .clk2(clk2), .val(write_data[1]), .load(nor_27_out), .nload(not_7_out), .ic(d_ff_1_qn));  // open: valout
  reg_bit_4 reg_bit_4_19 (
    .clk1(clk1), .clk2(clk2), .val(write_data[2]), .load(nor_27_out), .nload(not_7_out), .ic(d_ff_1_qn));  // open: valout
  reg_bit_4 reg_bit_4_20 (
    .clk1(clk1), .clk2(clk2), .val(write_data[3]), .load(nor_27_out), .nload(not_7_out), .ic(d_ff_1_qn));  // open: valout
  reg_bit_4 reg_bit_4_21 (
    .clk1(clk1), .clk2(clk2), .val(write_data[4]), .load(nor_27_out), .nload(not_7_out), .ic(d_ff_1_qn));  // open: valout
  reg_bit_4 reg_bit_4_22 (
    .clk1(clk1), .clk2(clk2), .val(write_data[5]), .load(nor_27_out), .nload(not_7_out), .ic(d_ff_1_qn));  // open: valout
  reg_bit_4 reg_bit_4_23 (
    .clk1(clk1), .clk2(clk2), .val(write_data[6]), .load(nor_27_out), .nload(not_7_out), .ic(d_ff_1_qn));  // open: valout
  reg_bit_4 reg_bit_4_24 (
    .clk1(clk1), .clk2(clk2), .val(write_data[7]), .load(nor_27_out), .nload(not_7_out), .ic(d_ff_1_qn));  // open: valout
  reg_bit_4 reg_bit_4_25 (
    .clk1(clk1), .clk2(clk2), .val(write_data[3]), .load(nor_28_out), .nload(not_8_out), .ic(d_ff_1_qn));  // open: valout
  reg_bit_4 reg_bit_4_26 (
    .clk1(clk1), .clk2(clk2), .val(write_data[4]), .load(nor_28_out), .nload(not_8_out), .ic(d_ff_1_qn));  // open: valout
  reg_bit_4 reg_bit_4_27 (
    .clk1(clk1), .clk2(clk2), .val(write_data[5]), .load(nor_28_out), .nload(not_8_out), .ic(d_ff_1_qn));  // open: valout
  reg_bit_4 reg_bit_4_28 (
    .clk1(clk1), .clk2(clk2), .val(write_data[7]), .load(nor_28_out), .nload(not_8_out), .ic(d_ff_1_qn));  // open: valout
  reg_bit_4 reg_bit_4_29 (
    .clk1(clk1), .clk2(clk2), .val(write_data[0]), .load(nor_29_out), .nload(not_9_out), .ic(d_ff_1_qn));  // open: valout
  reg_bit_4 reg_bit_4_30 (
    .clk1(clk1), .clk2(clk2), .val(write_data[1]), .load(nor_29_out), .nload(not_9_out), .ic(d_ff_1_qn));  // open: valout
  reg_bit_4 reg_bit_4_31 (
    .clk1(clk1), .clk2(clk2), .val(write_data[2]), .load(nor_29_out), .nload(not_9_out), .ic(d_ff_1_qn));  // open: valout
  reg_bit_4 reg_bit_4_32 (
    .clk1(clk1), .clk2(clk2), .val(write_data[3]), .load(nor_29_out), .nload(not_9_out), .ic(d_ff_1_qn));  // open: valout
  reg_bit_4 reg_bit_4_33 (
    .clk1(clk1), .clk2(clk2), .val(write_data[0]), .load(nor_30_out), .nload(not_10_out), .ic(d_ff_1_qn));  // open: valout
  reg_bit_4 reg_bit_4_34 (
    .clk1(clk1), .clk2(clk2), .val(write_data[1]), .load(nor_30_out), .nload(not_10_out), .ic(d_ff_1_qn));  // open: valout
  reg_bit_4 reg_bit_4_35 (
    .clk1(clk1), .clk2(clk2), .val(write_data[2]), .load(nor_30_out), .nload(not_10_out), .ic(d_ff_1_qn));  // open: valout
  reg_bit_4 reg_bit_4_36 (
    .clk1(clk1), .clk2(clk2), .val(write_data[3]), .load(nor_30_out), .nload(not_10_out), .ic(d_ff_1_qn));  // open: valout
  reg_bit_4 reg_bit_4_37 (
    .clk1(clk1), .clk2(clk2), .val(write_data[4]), .load(nor_30_out), .nload(not_10_out), .ic(d_ff_1_qn));  // open: valout
  reg_bit_4 reg_bit_4_38 (
    .clk1(clk1), .clk2(clk2), .val(write_data[5]), .load(nor_30_out), .nload(not_10_out), .ic(d_ff_1_qn));  // open: valout
  reg_bit_4 reg_bit_4_39 (
    .clk1(clk1), .clk2(clk2), .val(write_data[6]), .load(nor_30_out), .nload(not_10_out), .ic(d_ff_1_qn));  // open: valout
  reg_bit_4 reg_bit_4_40 (
    .clk1(clk1), .clk2(clk2), .val(write_data[7]), .load(nor_30_out), .nload(not_10_out), .ic(d_ff_1_qn));  // open: valout
  reg_bit_2 reg_bit_2_10 (
    .clk1(clk1), .clk2(clk2), .val(write_data[0]), .load(nor_31_out), .nload(not_11_out), .ic(d_ff_1_qn),
    .valout(reg_bit_2_10_valout));
  reg_bit_2 reg_bit_2_11 (
    .clk1(clk1), .clk2(clk2), .val(write_data[1]), .load(nor_31_out), .nload(not_11_out), .ic(d_ff_1_qn),
    .valout(reg_bit_2_11_valout));
  reg_bit_2 reg_bit_2_12 (
    .clk1(clk1), .clk2(clk2), .val(write_data[2]), .load(nor_31_out), .nload(not_11_out), .ic(d_ff_1_qn),
    .valout(reg_bit_2_12_valout));
  reg_bit_4 reg_bit_4_41 (
    .clk1(clk1), .clk2(clk2), .val(write_data[4]), .load(nor_31_out), .nload(not_11_out), .ic(d_ff_1_qn),
    .valout(reg_bit_4_41_valout));
  reg_bit_4 reg_bit_4_42 (
    .clk1(clk1), .clk2(clk2), .val(write_data[5]), .load(nor_31_out), .nload(not_11_out), .ic(d_ff_1_qn),
    .valout(reg_bit_4_42_valout));
  reg_bit_4 reg_bit_4_43 (
    .clk1(clk1), .clk2(clk2), .val(write_data[6]), .load(nor_31_out), .nload(not_11_out), .ic(d_ff_1_qn),
    .valout(reg_bit_4_43_valout));
  reg_bit_4 reg_bit_4_44 (
    .clk1(clk1), .clk2(clk2), .val(write_data[7]), .load(nor_31_out), .nload(not_11_out), .ic(d_ff_1_qn),
    .valout(reg_bit_4_44_valout));
  reg_bit_2 reg_bit_2_13 (
    .clk1(clk1), .clk2(clk2), .val(write_data[0]), .load(nor_32_out), .nload(not_12_out), .ic(d_ff_1_qn));  // open: valout
  reg_bit_2 reg_bit_2_14 (
    .clk1(clk1), .clk2(clk2), .val(write_data[1]), .load(nor_32_out), .nload(not_12_out), .ic(d_ff_1_qn));  // open: valout
  reg_bit_4 reg_bit_4_45 (
    .clk1(clk1), .clk2(clk2), .val(write_data[3]), .load(nor_32_out), .nload(not_12_out), .ic(d_ff_1_qn));  // open: valout
  reg_bit_2 reg_bit_2_15 (
    .clk1(clk1), .clk2(clk2), .val(write_data[4]), .load(nor_32_out), .nload(not_12_out), .ic(d_ff_1_qn));  // open: valout
  reg_bit_4 reg_bit_4_46 (
    .clk1(clk1), .clk2(clk2), .val(write_data[5]), .load(nor_32_out), .nload(not_12_out), .ic(d_ff_1_qn));  // open: valout
  reg_bit_2 reg_bit_2_16 (
    .clk1(clk1), .clk2(clk2), .val(write_data[6]), .load(nor_32_out), .nload(not_12_out), .ic(d_ff_1_qn));  // open: valout
  reg_bit_2 reg_bit_2_17 (
    .clk1(clk1), .clk2(clk2), .val(write_data[7]), .load(nor_32_out), .nload(not_12_out), .ic(d_ff_1_qn));  // open: valout
  not not_13 (not_13_out, reg_bit_2_10_valout);
  not not_14 (not_14_out, reg_bit_2_11_valout);
  not not_15 (not_15_out, reg_bit_2_12_valout);
  or or_1 (or_1_out, undriven, d_ff_24_qn);
  assign not_16_out = ~reg_bit_2_1_valout;  // NOT_Gate not_16, 9 bits wide
  and and_12 (and_12_out, cnt_bit_2_valout, not_13_out);
  and and_13 (and_13_out, cnt_bit_4_valout, not_14_out);
  and and_14 (and_14_out, cnt_bit_6_valout, not_15_out);
  and and_15 (and_15_out, cnt_bit_8_valout, 1'b0);
  and and_16 (and_16_out, op_reg_bank_sel, 1'b0);
  nor nor_33 (nor_33_out, not_13_out, not_14_out);
  nor nor_34 (nor_34_out, cnt_bit_2_valout, not_13_out);
  nor nor_35 (nor_35_out, cnt_bit_4_valout, not_14_out);
  nor nor_36 (nor_36_out, cnt_bit_6_valout, not_15_out);
  nor nor_37 (nor_37_out, cnt_bit_8_valout, 1'b0);
  nor nor_38 (nor_38_out, op_reg_bank_sel, 1'b0);
  not not_17 (not_17_out, d_ff_19_qn);
  and and_17 (and_17_out, not_17_out, d_ff_4_qn);
  or or_2 (or_2_out, and_17_out, undriven_7);
  not not_18 (not_18_out, data_wr);
  nor nor_39 (nor_39_out, IC, cnt_bit_9_cout);
  cnt_bit cnt_bit_1 (.cin(d_ff_23_q), .ic(IC), .clk1(clk1), .clk2(clk2), .cout(cnt_bit_1_cout));  // open: valout
  cnt_bit cnt_bit_2 (
    .cin(1'b1), .ic(or_1_out), .clk1(clk1), .clk2(clk2), .cout(cnt_bit_2_cout), .valout(cnt_bit_2_valout));
  sr_bit sr_bit_13 (.clk1(clk1), .clk2(clk2), .val(or_4_out), .valout(sr_bit_13_valout));  // open: nvalout
  sr_bit sr_bit_14 (
    .clk1(clk1), .clk2(clk2), .val(controlled_buffer_1_out), .valout(sr_bit_14_valout));  // open: nvalout
  sr_bit sr_bit_15 (
    .clk1(clk1), .clk2(clk2), .val(controlled_buffer_3_out), .valout(sr_bit_15_valout));  // open: nvalout
  sr_bit sr_bit_16 (
    .clk1(clk1), .clk2(clk2), .val(controlled_buffer_5_out), .valout(sr_bit_16_valout));  // open: nvalout
  D_Flip_Flop #(.trigger("high")) d_ff_4 (.D(undriven_5), .clk(clk2), .Qn(d_ff_4_qn));  // open: Q, preset, reset
  and and_18 (and_18_out, nor_39_out, d_ff_22_q);
  nor nor_40 (nor_40_out, and_12_out, nor_34_out, and_13_out, nor_35_out, and_14_out, nor_36_out, and_15_out, nor_37_out, and_16_out, nor_38_out, nor_33_out);
  sr_bit sr_bit_17 (.clk1(clk1), .clk2(clk2), .val(sr_bit_13_valout), .valout(sr_bit_17_valout));  // open: nvalout
  sr_bit sr_bit_18 (.clk1(clk1), .clk2(clk2), .val(sr_bit_14_valout), .valout(sr_bit_18_valout));  // open: nvalout
  sr_bit sr_bit_19 (.clk1(clk1), .clk2(clk2), .val(sr_bit_15_valout), .valout(sr_bit_19_valout));  // open: nvalout
  sr_bit sr_bit_20 (.clk1(clk1), .clk2(clk2), .val(sr_bit_16_valout), .valout(sr_bit_20_valout));  // open: nvalout
  D_Flip_Flop #(.trigger("high")) d_ff_5 (.D(nor_41_out), .clk(clk2), .Qn(d_ff_5_qn));  // open: Q, preset, reset
  nor nor_41 (nor_41_out, not_16_out[7], reg_bit_2_1_valout[6], not_16_out[5], not_16_out[4], undriven_9);
  D_Flip_Flop #(.trigger("high")) d_ff_6 (.D(nor_42_out), .clk(clk2), .Qn(d_ff_6_qn));  // open: Q, preset, reset
  nor nor_42 (nor_42_out, not_16_out[7], reg_bit_2_1_valout[6], reg_bit_2_1_valout[5], reg_bit_2_1_valout[4], undriven_9);
  D_Flip_Flop #(.trigger("high")) d_ff_7 (.D(nor_43_out), .clk(clk2), .Qn(d_ff_7_qn));  // open: Q, preset, reset
  nor nor_43 (nor_43_out, not_16_out[7], reg_bit_2_1_valout[6], not_16_out[5], reg_bit_2_1_valout[4], undriven_9);
  D_Flip_Flop #(.trigger("high")) d_ff_8 (.D(nor_44_out), .clk(clk2), .Qn(d_ff_8_qn));  // open: Q, preset, reset
  nor nor_44 (nor_44_out, not_16_out[7], reg_bit_2_1_valout[6], reg_bit_2_1_valout[5], not_16_out[4], undriven_9);
  D_Flip_Flop #(.trigger("high")) d_ff_9 (.D(nor_45_out), .clk(clk2), .Qn(d_ff_9_qn));  // open: Q, preset, reset
  nor nor_45 (nor_45_out, reg_bit_2_1_valout[7], not_16_out[6], not_16_out[5], not_16_out[4], undriven_9);
  D_Flip_Flop #(.trigger("high")) d_ff_10 (.D(nor_46_out), .clk(clk2), .Qn(d_ff_10_qn));  // open: Q, preset, reset
  nor nor_46 (nor_46_out, not_16_out[7], not_16_out[6], reg_bit_2_1_valout[5], reg_bit_2_1_valout[4], undriven_9);
  D_Flip_Flop #(.trigger("high")) d_ff_11 (.D(nor_47_out), .clk(clk2), .Qn(d_ff_11_qn));  // open: Q, preset, reset
  nor nor_47 (nor_47_out, reg_bit_2_1_valout[7], not_16_out[6], not_16_out[5], reg_bit_2_1_valout[4], undriven_9);
  D_Flip_Flop #(.trigger("high")) d_ff_12 (.D(nor_48_out), .clk(clk2), .Qn(d_ff_12_qn));  // open: Q, preset, reset
  nor nor_48 (nor_48_out, reg_bit_2_1_valout[7], not_16_out[6], reg_bit_2_1_valout[5], reg_bit_2_1_valout[4], not_16_out[3], not_16_out[2], undriven_8);
  D_Flip_Flop #(.trigger("high")) d_ff_13 (.D(nor_49_out), .clk(clk2), .Qn(d_ff_13_qn));  // open: Q, preset, reset
  nor nor_49 (nor_49_out, reg_bit_2_1_valout[7], not_16_out[6], reg_bit_2_1_valout[5], not_16_out[4], reg_bit_2_1_valout[3], reg_bit_2_1_valout[2], undriven_8);
  D_Flip_Flop #(.trigger("high")) d_ff_14 (.D(nor_50_out), .clk(clk2), .Qn(d_ff_14_qn));  // open: Q, preset, reset
  nor nor_50 (nor_50_out, reg_bit_2_1_valout[7], not_16_out[6], reg_bit_2_1_valout[5], not_16_out[4], not_16_out[3], not_16_out[2], undriven_8);
  D_Flip_Flop #(.trigger("high")) d_ff_15 (.D(nor_51_out), .clk(clk2), .Qn(d_ff_15_qn));  // open: Q, preset, reset
  nor nor_51 (nor_51_out, reg_bit_2_1_valout[7], not_16_out[6], reg_bit_2_1_valout[5], not_16_out[4], not_16_out[3], reg_bit_2_1_valout[2], undriven_8);
  D_Flip_Flop #(.trigger("high")) d_ff_16 (.D(nor_52_out), .clk(clk2), .Qn(d_ff_16_qn));  // open: Q, preset, reset
  nor nor_52 (nor_52_out, reg_bit_2_1_valout[7], not_16_out[6], reg_bit_2_1_valout[5], not_16_out[4], reg_bit_2_1_valout[3], not_16_out[2], undriven_8);
  D_Flip_Flop #(.trigger("high")) d_ff_17 (.D(nor_53_out), .clk(clk2), .Qn(d_ff_17_qn));  // open: Q, preset, reset
  nor nor_53 (nor_53_out, reg_bit_2_1_valout[7], not_16_out[6], reg_bit_2_1_valout[5], reg_bit_2_1_valout[4], not_16_out[3], reg_bit_2_1_valout[2], undriven_8);
  nor nor_54 (nor_54_out, not_18_out, and_18_out);
  D_Flip_Flop #(.trigger("high")) d_ff_18 (
    .D(nor_40_out), .clk(clk2), .Q(d_ff_18_q), .Qn(d_ff_18_qn));  // open: preset, reset
  sr_bit sr_bit_21 (.clk1(clk1), .clk2(clk2), .val(sr_bit_17_valout), .valout(sr_bit_21_valout));  // open: nvalout
  sr_bit sr_bit_22 (.clk1(clk1), .clk2(clk2), .val(sr_bit_18_valout), .valout(sr_bit_22_valout));  // open: nvalout
  sr_bit sr_bit_23 (.clk1(clk1), .clk2(clk2), .val(sr_bit_19_valout), .valout(sr_bit_23_valout));  // open: nvalout
  sr_bit sr_bit_24 (.clk1(clk1), .clk2(clk2), .val(sr_bit_20_valout), .valout(sr_bit_24_valout));  // open: nvalout
  D_Flip_Flop #(.trigger("high")) d_ff_19 (
    .D(undriven_4), .clk(nor_55_out), .Qn(d_ff_19_qn));  // open: Q, preset, reset
  D_Flip_Flop #(.trigger("high")) d_ff_20 (.D(d_ff_4_qn), .clk(clk1), .Qn(d_ff_20_qn));  // open: Q, preset, reset
  D_Flip_Flop #(.trigger("high")) d_ff_21 (.D(nor_54_out), .clk(clk1), .Qn(d_ff_21_qn));  // open: Q, preset, reset
  cnt_bit cnt_bit_3 (.cin(cnt_bit_1_cout), .ic(IC), .clk1(clk1), .clk2(clk2), .cout(cnt_bit_3_cout));  // open: valout
  cnt_bit cnt_bit_4 (
    .cin(cnt_bit_2_cout), .ic(or_1_out), .clk1(clk1), .clk2(clk2), .valout(cnt_bit_4_valout));  // open: cout
  sr_bit sr_bit_25 (.clk1(clk1), .clk2(clk2), .val(sr_bit_21_valout), .valout(sr_bit_25_valout));  // open: nvalout
  sr_bit sr_bit_26 (.clk1(clk1), .clk2(clk2), .val(sr_bit_22_valout), .valout(sr_bit_26_valout));  // open: nvalout
  sr_bit sr_bit_27 (.clk1(clk1), .clk2(clk2), .val(sr_bit_23_valout), .valout(sr_bit_27_valout));  // open: nvalout
  sr_bit sr_bit_28 (.clk1(clk1), .clk2(clk2), .val(sr_bit_24_valout), .valout(sr_bit_28_valout));  // open: nvalout
  timer_bit timer_bit_1 (
    .cin(or_2_out), .ic(d_ff_19_qn), .load(nand_3_out), .value(undriven_6[0]), .clk1(clk1), .clk2(clk2),
    .out_7(timer_bit_1_out_7));
  timer_bit timer_bit_2 (
    .cin(timer_bit_9_out_7), .ic(d_ff_19_qn), .load(nand_3_out), .value(undriven_6[5]), .clk1(clk1),
    .clk2(clk2), .out_7(timer_bit_2_out_7));
  D_Flip_Flop #(.trigger("high")) d_ff_22 (.D(d_ff_21_qn), .clk(clk2), .Q(d_ff_22_q));  // open: Qn, preset, reset
  D_Flip_Flop #(.trigger("high")) d_ff_23 (.D(d_ff_21_qn), .clk(clk2), .Q(d_ff_23_q));  // open: Qn, preset, reset
  D_Flip_Flop #(.trigger("high")) d_ff_24 (.D(cnt_bit_4_valout), .Qn(d_ff_24_qn));  // open: clk, Q, preset, reset
  sr_bit sr_bit_29 (.clk1(clk1), .clk2(clk2), .val(d_ff_19_qn), .nvalout(sr_bit_29_nvalout));  // open: valout
  D_Flip_Flop #(.trigger("high")) d_ff_25 (.D(d_ff_20_qn), .clk(clk2), .Q(d_ff_25_q));  // open: Qn, preset, reset
  not not_19 (busy, d_ff_21_qn);
  sr_bit sr_bit_30 (.clk1(clk1), .clk2(clk2), .val(sr_bit_25_valout), .valout(sr_bit_30_valout));  // open: nvalout
  sr_bit sr_bit_31 (.clk1(clk1), .clk2(clk2), .val(sr_bit_26_valout), .valout(sr_bit_31_valout));  // open: nvalout
  sr_bit sr_bit_32 (.clk1(clk1), .clk2(clk2), .val(sr_bit_27_valout), .valout(sr_bit_32_valout));  // open: nvalout
  D_Flip_Flop #(.trigger("high")) d_ff_26 (
    .D(sr_bit_33_valout), .clk(clk1), .Qn(d_ff_26_qn));  // open: Q, preset, reset
  sr_bit sr_bit_33 (.clk1(clk1), .clk2(clk2), .val(sr_bit_28_valout), .valout(sr_bit_33_valout));  // open: nvalout
  or or_3 (or_3_out, sr_bit_29_nvalout, d_ff_19_qn);
  nor nor_55 (nor_55_out, d_ff_20_qn, d_ff_25_q);
  cnt_bit cnt_bit_5 (.cin(cnt_bit_3_cout), .ic(IC), .clk1(clk1), .clk2(clk2), .cout(cnt_bit_5_cout));  // open: valout
  sr_bit sr_bit_34 (.clk1(clk1), .clk2(clk2), .val(sr_bit_30_valout), .valout(sr_bit_34_valout));  // open: nvalout
  sr_bit sr_bit_35 (.clk1(clk1), .clk2(clk2), .val(sr_bit_31_valout), .valout(sr_bit_35_valout));  // open: nvalout
  sr_bit sr_bit_36 (.clk1(clk1), .clk2(clk2), .val(sr_bit_32_valout), .valout(sr_bit_36_valout));  // open: nvalout
  D_Flip_Flop #(.trigger("high")) d_ff_27 (.D(d_ff_26_qn), .clk(clk2), .Qn(d_ff_27_qn));  // open: Q, preset, reset
  D_Flip_Flop #(.trigger("high")) d_ff_28 (.D(d_ff_26_qn), .clk(clk2), .Q(d_ff_28_q));  // open: Qn, preset, reset
  sr_bit sr_bit_37 (.clk1(clk1), .clk2(clk2), .val(timer_bit_10_out_7), .nvalout(sr_bit_37_nvalout));  // open: valout
  timer_bit timer_bit_3 (
    .cin(timer_bit_1_out_7), .ic(d_ff_19_qn), .load(nand_3_out), .value(undriven_6[1]), .clk1(clk1),
    .clk2(clk2), .out_7(timer_bit_3_out_7));
  timer_bit timer_bit_4 (
    .cin(timer_bit_2_out_7), .ic(d_ff_19_qn), .load(nand_3_out), .value(undriven_6[6]), .clk1(clk1),
    .clk2(clk2), .out_7(timer_bit_4_out_7));
  cnt_bit cnt_bit_6 (
    .cin(d_ff_24_qn), .ic(undriven), .clk1(clk1), .clk2(clk2), .cout(cnt_bit_6_cout),
    .valout(cnt_bit_6_valout));
  not not_20 (not_20_out, IC);
  nand nand_3 (nand_3_out, or_3_out, sr_bit_37_nvalout);
  assign controlled_buffer_1_out = d_ff_18_qn ? sr_bit_34_valout : 1'bz;  // Controlled_Buffer controlled_buffer_1
  assign controlled_buffer_1_out = d_ff_18_q ? reg_bit_4_44_valout : 1'bz;  // Controlled_Buffer controlled_buffer_2
  assign controlled_buffer_3_out = d_ff_18_qn ? sr_bit_35_valout : 1'bz;  // Controlled_Buffer controlled_buffer_3
  assign controlled_buffer_3_out = d_ff_18_q ? reg_bit_4_42_valout : 1'bz;  // Controlled_Buffer controlled_buffer_4
  assign controlled_buffer_5_out = d_ff_18_qn ? sr_bit_36_valout : 1'bz;  // Controlled_Buffer controlled_buffer_5
  assign controlled_buffer_5_out = d_ff_18_q ? reg_bit_4_43_valout : 1'bz;  // Controlled_Buffer controlled_buffer_6
  and and_19 (and_19_out, d_ff_18_q, reg_bit_4_41_valout);
  or or_4 (or_4_out, and_19_out, and_20_out);
  and and_20 (and_20_out, d_ff_18_qn, not_20_out, d_ff_27_qn);
  D_Flip_Flop #(.trigger("high")) d_ff_29 (.D(undriven_2), .clk(clk2), .Qn(d_ff_29_qn));  // open: Q, preset, reset
  not not_21 (not_21_out, nand_3_out);
  D_Flip_Flop #(.trigger("high")) d_ff_30 (.D(undriven_3), .clk(clk2), .Q(d_ff_30_q));  // open: Qn, preset, reset
  not not_22 (not_22_out, sr_bit_37_nvalout);
  not not_23 (not_23_out, undriven_10);
  cnt_bit cnt_bit_7 (.cin(cnt_bit_5_cout), .ic(IC), .clk1(clk1), .clk2(clk2), .cout(cnt_bit_7_cout));  // open: valout
  not not_24 (not_24_out, not_22_out);
  not not_25 (not_25_out, undriven_11);
  nor nor_56 (nor_56_out, not_21_out, d_ff_30_q);
  D_Flip_Flop #(.trigger("high")) d_ff_31 (.D(nor_56_out), .clk(nor_55_out), .Q(d_ff_31_q));  // open: Qn, preset, reset
  nor nor_57 (nor_57_out, not_24_out, not_23_out, not_25_out);
  timer_bit timer_bit_5 (
    .cin(timer_bit_3_out_7), .ic(d_ff_19_qn), .load(nand_3_out), .value(undriven_6[2]), .clk1(clk1),
    .clk2(clk2), .out_7(timer_bit_5_out_7));
  timer_bit timer_bit_6 (
    .cin(timer_bit_4_out_7), .ic(d_ff_19_qn), .load(nand_3_out), .value(undriven_6[7]), .clk1(clk1),
    .clk2(clk2), .out_7(timer_bit_6_out_7));
  cnt_bit cnt_bit_8 (
    .cin(cnt_bit_6_cout), .ic(undriven), .clk1(clk1), .clk2(clk2), .cout(cnt_bit_8_cout),
    .valout(cnt_bit_8_valout));
  and and_21 (and_21_out, not_23_out, d_ff_33_q);
  cnt_bit cnt_bit_9 (.cin(cnt_bit_7_cout), .ic(IC), .clk1(clk1), .clk2(clk2), .cout(cnt_bit_9_cout));  // open: valout
  nand nand_4 (keyon_csm, d_ff_29_qn, d_ff_31_q);
  nor nor_58 (nor_58_out, nor_57_out, and_21_out);
  D_Flip_Flop #(.trigger("high")) d_ff_32 (.D(nor_58_out), .clk(clk1), .Qn(timer_a_status));  // open: Q, preset, reset
  D_Flip_Flop #(.trigger("high")) d_ff_33 (.D(timer_a_status), .clk(clk2), .Q(d_ff_33_q));  // open: Qn, preset, reset
  timer_bit timer_bit_7 (
    .cin(timer_bit_5_out_7), .ic(d_ff_19_qn), .load(nand_3_out), .value(undriven_6[3]), .clk1(clk1),
    .clk2(clk2), .out_7(timer_bit_7_out_7));
  timer_bit timer_bit_8 (
    .cin(timer_bit_6_out_7), .ic(d_ff_19_qn), .load(nand_3_out), .value(undriven_6[8]), .clk1(clk1),
    .clk2(clk2), .out_7(timer_bit_8_out_7));
  cnt_bit cnt_bit_10 (
    .cin(cnt_bit_8_cout), .ic(undriven), .clk1(clk1), .clk2(clk2), .valout(op_reg_bank_sel));  // open: cout
  nand nand_5 (keyon, d_ff_28_q, keyon_csm);
  timer_bit timer_bit_9 (
    .cin(timer_bit_7_out_7), .ic(d_ff_19_qn), .load(nand_3_out), .value(undriven_6[4]), .clk1(clk1),
    .clk2(clk2), .out_7(timer_bit_9_out_7));
  timer_bit timer_bit_10 (
    .cin(timer_bit_8_out_7), .ic(d_ff_19_qn), .load(nand_3_out), .value(undriven_6[9]), .clk1(clk1),
    .clk2(clk2), .out_7(timer_bit_10_out_7));
endmodule

module io_ctrl (
  input  RD,
  input  WR,
  input  A0,
  input  A1,
  input  CS,
  input  IC,
  input  clk1,
  input  clk2,
  input  aclk1,
  input  aclk2,
  output addr_wr,
  output data_wr,
  output data_wr2,
  output read,
  output read0,
  output read1,
  output read2,
  output write,
  output write0,
  output write1,
  output out_21,
  output out_22
);

  wire and_1_out, and_2_out, and_3_out, and_4_out, and_5_out, and_6_out, d_ff_1_qn, d_ff_2_qn, d_ff_3_qn,
       nand_1_out, nor_1_out, nor_2_out, nor_3_out, nor_4_out, nor_5_out, nor_6_out, nor_7_out, nor_8_out,
       nor_9_out, nor_10_out, nor_11_out, nor_12_out, nor_13_out, nor_14_out, nor_15_out, nor_16_out,
       nor_17_out, nor_18_out, nor_19_out, nor_20_out, nor_21_out, nor_22_out, nor_23_out, nor_24_out,
       nor_25_out, nor_26_out, not_1_out, not_2_out, not_3_out, not_4_out, not_5_out, not_6_out, not_7_out,
       not_8_out, not_9_out, not_10_out, not_11_out, not_12_out, not_13_out, not_18_out, not_22_out,
       not_23_out, not_24_out, not_25_out, or_1_out, sr_bit_1_valout, sr_bit_2_valout, sr_bit_3_valout;

  not not_1 (not_1_out, RD);
  not not_2 (not_2_out, not_1_out);
  not not_3 (not_3_out, WR);
  not not_4 (not_4_out, not_3_out);
  not not_5 (not_5_out, A0);
  not not_6 (not_6_out, not_5_out);
  not not_7 (not_7_out, A1);
  not not_8 (not_8_out, not_7_out);
  not not_9 (not_9_out, CS);
  not not_10 (not_10_out, not_9_out);
  not not_11 (not_11_out, nor_22_out);
  not not_12 (not_12_out, not_18_out);
  not not_13 (not_13_out, not_18_out);
  nor nor_1 (nor_1_out, not_11_out, nor_2_out);
  nor nor_2 (nor_2_out, nor_1_out, d_ff_1_qn);
  nor nor_3 (nor_3_out, not_12_out, nor_4_out);
  nor nor_4 (nor_4_out, nor_3_out, d_ff_2_qn);
  nor nor_5 (nor_5_out, not_13_out, nor_6_out);
  nor nor_6 (nor_6_out, nor_5_out, d_ff_3_qn);
  and and_1 (and_1_out, clk1, nor_2_out);
  and and_2 (and_2_out, clk1, nor_1_out);
  and and_3 (and_3_out, clk1, nor_4_out);
  and and_4 (and_4_out, clk1, nor_3_out);
  and and_5 (and_5_out, aclk1, nor_6_out);
  and and_6 (and_6_out, aclk1, nor_5_out);
  nor nor_7 (nor_7_out, not_2_out, IC, not_10_out);
  nor nor_8 (nor_8_out, not_4_out, not_6_out, not_10_out);
  nor nor_9 (nor_9_out, not_2_out, IC, not_8_out, not_5_out, not_10_out);
  nor nor_10 (nor_10_out, not_4_out, IC, not_8_out, not_5_out, not_10_out);
  nor nor_11 (nor_11_out, not_4_out, IC, not_6_out, not_8_out, not_10_out);
  nor nor_12 (nor_12_out, not_4_out, IC, not_5_out, not_10_out);
  nor nor_13 (nor_13_out, not_2_out, IC, not_6_out, not_7_out, not_10_out);
  nor nor_14 (nor_14_out, not_2_out, IC, not_6_out, not_8_out, not_10_out);
  nor nor_15 (nor_15_out, not_4_out, not_10_out);
  nor nor_16 (nor_16_out, and_1_out, nor_17_out);
  nor nor_17 (nor_17_out, and_2_out, nor_16_out);
  nor nor_18 (nor_18_out, and_3_out, nor_19_out);
  nor nor_19 (nor_19_out, and_4_out, nor_18_out);
  nor nor_20 (nor_20_out, and_5_out, nor_21_out);
  nor nor_21 (nor_21_out, and_6_out, nor_20_out);
  not not_14 (read, nor_7_out);
  not not_15 (read1, nor_9_out);
  not not_16 (write1, nor_10_out);
  not not_17 (write0, nor_11_out);
  not not_18 (not_18_out, nor_12_out);
  not not_19 (read2, nor_13_out);
  not not_20 (read0, nor_14_out);
  not not_21 (write, nor_15_out);
  D_Flip_Flop #(.trigger("high")) d_ff_1 (.D(nor_16_out), .clk(clk2), .Qn(d_ff_1_qn));  // open: Q, preset, reset
  D_Flip_Flop #(.trigger("high")) d_ff_2 (.D(nor_18_out), .clk(clk2), .Qn(d_ff_2_qn));  // open: Q, preset, reset
  D_Flip_Flop #(.trigger("high")) d_ff_3 (.D(nor_20_out), .clk(aclk2), .Qn(d_ff_3_qn));  // open: Q, preset, reset
  nor nor_22 (nor_22_out, IC, nor_8_out);
  sr_bit sr_bit_1 (.clk1(clk1), .clk2(clk2), .val(d_ff_1_qn), .valout(sr_bit_1_valout));  // open: nvalout
  sr_bit sr_bit_2 (.clk1(clk1), .clk2(clk2), .val(d_ff_2_qn), .valout(sr_bit_2_valout));  // open: nvalout
  sr_bit sr_bit_3 (.clk1(aclk1), .clk2(aclk2), .val(d_ff_3_qn), .valout(sr_bit_3_valout));  // open: nvalout
  not not_22 (not_22_out, d_ff_1_qn);
  not not_23 (not_23_out, d_ff_2_qn);
  not not_24 (not_24_out, d_ff_3_qn);
  or or_1 (or_1_out, not_18_out, not_8_out);
  not not_25 (not_25_out, IC);
  nor nor_23 (nor_23_out, sr_bit_1_valout, not_22_out);
  nor nor_24 (nor_24_out, sr_bit_2_valout, not_23_out);
  nor nor_25 (nor_25_out, sr_bit_3_valout, not_24_out);
  not not_26 (out_21, nor_26_out);
  nor nor_26 (nor_26_out, nor_22_out, not_8_out);
  not not_27 (out_22, nand_1_out);
  nand nand_1 (nand_1_out, or_1_out, not_25_out);
  not not_28 (addr_wr, nor_23_out);
  not not_29 (data_wr, nor_24_out);
  not not_30 (data_wr2, nor_25_out);
endmodule

module io_ctrl_2612 (
  input  RD,
  input  WR,
  input  A0,
  input  A1,
  input  CS,
  input  IC,
  input  clk1,
  input  clk2,
  output addr_wr,
  output data_wr,
  output read,
  output read0,
  output write
);

  wire and_1_out, and_2_out, and_3_out, and_4_out, d_ff_1_qn, d_ff_2_qn, nor_1_out, nor_2_out, nor_3_out,
       nor_4_out, nor_5_out, nor_6_out, nor_7_out, nor_8_out, nor_9_out, nor_10_out, nor_11_out, nor_12_out,
       nor_13_out, nor_14_out, nor_15_out, nor_16_out, not_1_out, not_2_out, not_3_out, not_4_out, not_5_out,
       not_6_out, not_7_out, not_8_out, not_9_out, not_10_out, not_11_out, not_12_out, not_14_out,
       not_17_out, not_18_out, sr_bit_1_valout, sr_bit_2_valout;

  not not_1 (not_1_out, RD);
  not not_2 (not_2_out, not_1_out);
  not not_3 (not_3_out, WR);
  not not_4 (not_4_out, not_3_out);
  not not_5 (not_5_out, A0);
  not not_6 (not_6_out, not_5_out);
  not not_7 (not_7_out, A1);
  not not_8 (not_8_out, not_7_out);
  not not_9 (not_9_out, CS);
  not not_10 (not_10_out, not_9_out);
  not not_11 (not_11_out, nor_14_out);
  not not_12 (not_12_out, not_14_out);
  nor nor_1 (nor_1_out, not_11_out, nor_2_out);
  nor nor_2 (nor_2_out, nor_1_out, d_ff_1_qn);
  nor nor_3 (nor_3_out, not_12_out, nor_4_out);
  nor nor_4 (nor_4_out, nor_3_out, d_ff_2_qn);
  and and_1 (and_1_out, clk1, nor_2_out);
  and and_2 (and_2_out, clk1, nor_1_out);
  and and_3 (and_3_out, clk1, nor_4_out);
  and and_4 (and_4_out, clk1, nor_3_out);
  nor nor_5 (nor_5_out, not_2_out, IC, not_10_out);
  nor nor_6 (nor_6_out, not_4_out, not_6_out, not_10_out);
  nor nor_7 (nor_7_out, not_4_out, IC, not_5_out, not_10_out);
  nor nor_8 (nor_8_out, not_2_out, IC, not_6_out, not_8_out, not_10_out);
  nor nor_9 (nor_9_out, not_4_out, not_10_out);
  nor nor_10 (nor_10_out, and_1_out, nor_11_out);
  nor nor_11 (nor_11_out, and_2_out, nor_10_out);
  nor nor_12 (nor_12_out, and_3_out, nor_13_out);
  nor nor_13 (nor_13_out, and_4_out, nor_12_out);
  not not_13 (read, nor_5_out);
  not not_14 (not_14_out, nor_7_out);
  not not_15 (read0, nor_8_out);
  not not_16 (write, nor_9_out);
  D_Flip_Flop #(.trigger("high")) d_ff_1 (.D(nor_10_out), .clk(clk2), .Qn(d_ff_1_qn));  // open: Q, preset, reset
  D_Flip_Flop #(.trigger("high")) d_ff_2 (.D(nor_12_out), .clk(clk2), .Qn(d_ff_2_qn));  // open: Q, preset, reset
  nor nor_14 (nor_14_out, IC, nor_6_out);
  sr_bit sr_bit_1 (.clk1(clk1), .clk2(clk2), .val(d_ff_1_qn), .valout(sr_bit_1_valout));  // open: nvalout
  sr_bit sr_bit_2 (.clk1(clk1), .clk2(clk2), .val(d_ff_2_qn), .valout(sr_bit_2_valout));  // open: nvalout
  not not_17 (not_17_out, d_ff_1_qn);
  not not_18 (not_18_out, d_ff_2_qn);
  nor nor_15 (nor_15_out, sr_bit_1_valout, not_17_out);
  nor nor_16 (nor_16_out, sr_bit_2_valout, not_18_out);
  not not_19 (addr_wr, nor_15_out);
  not not_20 (data_wr, nor_16_out);
endmodule

module reg_bit_2 (
  input  clk1,
  input  clk2,
  input  val,
  input  load,
  input  nload,
  input  ic,
  output valout
);

  wire controlled_buffer_1_out, d_ff_1_q, d_ff_2_qn;

  assign controlled_buffer_1_out = load ? val : 1'bz;  // Controlled_Buffer controlled_buffer_1
  assign controlled_buffer_1_out = nload ? d_ff_2_qn : 1'bz;  // Controlled_Buffer controlled_buffer_2
  D_Flip_Flop #(.trigger("high")) d_ff_1 (
    .D(controlled_buffer_1_out), .clk(clk1), .Q(d_ff_1_q));  // open: Qn, preset, reset
  nand nand_1 (valout, d_ff_1_q, ic);
  D_Flip_Flop #(.trigger("high")) d_ff_2 (.D(valout), .clk(clk2), .Qn(d_ff_2_qn));  // open: Q, preset, reset
endmodule

module reg_bit_3 (
  input  clk1,
  input  clk2,
  input  val,
  input  load,
  input  nload,
  input  ic,
  output valout
);

  wire controlled_buffer_1_out, d_ff_1_q, d_ff_2_qn, nand_1_out;

  assign controlled_buffer_1_out = load ? val : 1'bz;  // Controlled_Buffer controlled_buffer_1
  assign controlled_buffer_1_out = nload ? d_ff_2_qn : 1'bz;  // Controlled_Buffer controlled_buffer_2
  D_Flip_Flop #(.trigger("high")) d_ff_1 (
    .D(controlled_buffer_1_out), .clk(clk1), .Q(d_ff_1_q));  // open: Qn, preset, reset
  nand nand_1 (nand_1_out, d_ff_1_q, ic);
  D_Flip_Flop #(.trigger("high")) d_ff_2 (.D(nand_1_out), .clk(clk2), .Qn(d_ff_2_qn));  // open: Q, preset, reset
  not not_1 (valout, d_ff_2_qn);
endmodule

module reg_bit_4 (
  input  clk1,
  input  clk2,
  input  val,
  input  load,
  input  nload,
  input  ic,
  output valout
);

  wire controlled_buffer_1_out, d_ff_1_q, nand_1_out;

  assign controlled_buffer_1_out = load ? val : 1'bz;  // Controlled_Buffer controlled_buffer_1
  assign controlled_buffer_1_out = nload ? valout : 1'bz;  // Controlled_Buffer controlled_buffer_2
  D_Flip_Flop #(.trigger("high")) d_ff_1 (
    .D(controlled_buffer_1_out), .clk(clk1), .Q(d_ff_1_q));  // open: Qn, preset, reset
  nand nand_1 (nand_1_out, d_ff_1_q, ic);
  D_Flip_Flop #(.trigger("high")) d_ff_2 (.D(nand_1_out), .clk(clk2), .Qn(valout));  // open: Q, preset, reset
endmodule

module cnt_bit (
  input  cin,
  input  ic,
  input  clk1,
  input  clk2,
  output cout,
  output valout
);

  wire and_1_out, d_ff_2_q, nor_2_out, not_1_out;

  not not_1 (not_1_out, cin);
  and and_1 (and_1_out, not_1_out, d_ff_2_q);
  nor nor_1 (cout, not_1_out, d_ff_2_q);
  nor nor_2 (nor_2_out, cout, ic, and_1_out);
  D_Flip_Flop #(.trigger("high")) d_ff_1 (.D(nor_2_out), .clk(clk1), .Qn(valout));  // open: Q, preset, reset
  D_Flip_Flop #(.trigger("high")) d_ff_2 (.D(valout), .clk(clk2), .Q(d_ff_2_q));  // open: Qn, preset, reset
endmodule

module timer_bit (
  input  cin,
  input  ic,
  input  load,
  input  value,
  input  clk1,
  input  clk2,
  output out_7
);

  wire and_1_out, and_2_out, d_ff_1_q, d_ff_2_q, d_ff_3_q, d_ff_4_q, nor_2_out, nor_3_out, not_1_out;

  not not_1 (not_1_out, cin);
  nor nor_1 (out_7, d_ff_4_q, not_1_out);
  and and_1 (and_1_out, not_1_out, d_ff_4_q);
  D_Flip_Flop #(.trigger("high")) d_ff_1 (.D(nor_2_out), .clk(clk1), .Q(d_ff_1_q));  // open: Qn, preset, reset
  nor nor_2 (nor_2_out, out_7, and_1_out, ic, load);
  D_Flip_Flop #(.trigger("high")) d_ff_2 (.D(load), .clk(clk1), .Q(d_ff_2_q));  // open: Qn, preset, reset
  D_Flip_Flop #(.trigger("high")) d_ff_3 (.D(value), .clk(clk1), .Q(d_ff_3_q));  // open: Qn, preset, reset
  nor nor_3 (nor_3_out, d_ff_1_q, and_2_out);
  and and_2 (and_2_out, d_ff_2_q, d_ff_3_q);
  D_Flip_Flop #(.trigger("high")) d_ff_4 (.D(nor_3_out), .clk(clk2), .Q(d_ff_4_q));  // open: Qn, preset, reset
endmodule
